# Fritzing sketch L298N Circuit (saved by Fritzing 0.9.3b)

parts:
  Arduino_UNO = Arduino Uno (Rev3)
  L298N = L298_BRIDGE_DRIVER [package=powerso20]
  VCC1 = Battery
  VCC2 = Battery
  VCC3 = Battery
  VCC4 = Battery
  M3 = DC Motor
  M4 = DC Motor
  M5 = DC Motor
  M6 = DC Motor
  U3 = HC-SR04 [chip_label=IC package="SIP (Single Inline) [THT]"]
  U4 = NodeMCU V1.0

nets:
  N1: Arduino_UNO.D9_PWM, L298N.IN4
  N2: Arduino_UNO.D10_PWM/SS, L298N.ENA
  N3: Arduino_UNO.D11_PWM/MOSI, L298N.ENB
  N4: Arduino_UNO.D12/MISO, U4.RX
  N5: Arduino_UNO.D13/SCK, U4.TX
  GND: Arduino_UNO.GND, L298N.GND, VCC4.-, U3.GND, U4.GND
  N6: Arduino_UNO.D0/RX, U3.Trig
  N7: Arduino_UNO.D1/TX, U3.Echo
  N8: Arduino_UNO.D3_PWM, L298N.IN1
  N9: Arduino_UNO.D5_PWM, L298N.IN2
  N10: Arduino_UNO.D6_PWM, L298N.IN3
  3V3: Arduino_UNO.3V3, U3.Vcc, U4.3V3
  5V: Arduino_UNO.5V, L298N.VSS
  N11: L298N.OUT1, M3.pin_1, M4.pin_1
  N12: L298N.OUT2, M3.pin_2, M4.pin_2
  N13: L298N.VS, VCC1.+
  N14: L298N.OUT3, M5.pin_1, M6.pin_1
  N15: L298N.OUT4, M5.pin_2, M6.pin_2
  N16: VCC1.-, VCC2.+
  N17: VCC2.-, VCC3.+
  N18: VCC3.-, VCC4.+

custom parts:
  HC-SR04: HC-SR04 ultrasound distance sensor
  NodeMCU V1.0: ESP8266 based NodeMCU
